# Fritzing sketch Circuit 7 (saved by Fritzing 0.9.3b)

parts:
  Part1 = Arduino Leonardo (Rev3b)
  microSD1 = MicroSD Card Module
  Part2 = Arduino Due (Rev2b)

nets:
  N1: Part1.SDA, Part2.D20/SDA3
  N2: Part1.SCL, Part2.D21/SCL3
  GND: microSD1.GND, Part2.GND
  VCC: microSD1.VCC, Part2.5V
  N3: microSD1.CS, Part2.D2_PWM

notes:
  TO USB keyboard
  Power/Serial debugging
  TO Host
